# Fritzing sketch button_debounce_zero (saved by Fritzing 0.9.3b)

parts:
  Raspberry_Pi_Zero2 = Raspberry Pi Zero
  S2 = Momentary Switch [package=ksa_sealed_tac_switch]
  C1 = Ceramic Capacitor [capacitance=100nF package="100 mil [THT, multilayer]"]  # not connected
  R1 = Resistor [tolerance=±5% resistance=1k package=THT]
  R2 = Resistor [tolerance=±5% resistance=10k package=THT]

nets:
  N1: Raspberry_Pi_Zero2.3V3, R1.Pin_1
  N2: Raspberry_Pi_Zero2.GND, R2.Pin_1
  N3: Raspberry_Pi_Zero2.GPIO24, S2.1, R2.Pin_0
  N4: S2.3, R1.Pin_0
