# Fritzing sketch complete circuit (saved by Fritzing 0.9.3b)
breadboards: 1

parts:
  Part2 = Adafruit Quad AlphaNumeric Featherwing - White [part_number="Adafruit #3127"]
  Raspberry_Pi_Zero1 = Raspberry Pi Zero
  SP1 = SPEAKER [package=pcb_mount_speaker]  # not connected
  R8 = Resistor [tolerance=±5% resistance=270 package=THT]
  R9 = Resistor [tolerance=±5% resistance=270 package=THT]
  C8 = Ceramic Capacitor [capacitance=10nF package="100 mil [THT, multilayer]"]
  C9 = Ceramic Capacitor [capacitance=10nF package="100 mil [THT, multilayer]"]
  R10 = Resistor [tolerance=±5% resistance=150 package=THT]
  R11 = Resistor [tolerance=±5% resistance=150 package=THT]
  C10 = Electrolytic Capacitor [capacitance=1µF package="100 mil [THT, electrolytic]"]
  C11 = Electrolytic Capacitor [capacitance=1µF package="100 mil [THT, electrolytic]"]
  S3 = Momentary Switch [package=ksa_sealed_tac_switch]
  C12 = Ceramic Capacitor [capacitance=100nF package="100 mil [THT, multilayer]"]  # not connected
  R12 = Resistor [tolerance=±5% resistance=10k package=THT]
  R13 = Resistor [tolerance=±5% resistance=1k package=THT]
  R14 = Photocell (LDR) [package=THT]
  C13 = Ceramic Capacitor [capacitance=1µF package="0603 [SMD, multilayer]"]

nets:
  GND: Part2.GND, Raspberry_Pi_Zero1.GND, C8.1, C9.0, R10.Pin_1, R11.Pin_0, R12.Pin_1
  3V3: Part2.VDD, Raspberry_Pi_Zero1.3v3, Raspberry_Pi_Zero1.3V3, R13.Pin_1
  N1: Part2.SCL, Raspberry_Pi_Zero1.GPIO3
  N2: Part2.SDA, Raspberry_Pi_Zero1.GPIO2
  N3: Raspberry_Pi_Zero1.GPIO20, R14.pin_0, C13.1
  N4: Raspberry_Pi_Zero1.GPIO24, S3.3, R12.Pin_0
  N5: Raspberry_Pi_Zero1.GPIO18, R9.Pin_0
  N6: R8.Pin_1, C8.0, R10.Pin_0, C11.+
  N7: R9.Pin_1, C9.1, R11.Pin_1, C10.+
  N8: S3.1, R13.Pin_0

custom parts:
  Adafruit Quad AlphaNumeric Featherwing - White: This is the White Adafruit 0.54" Dual Alphanumeric Display w/ FeatherWing Combo Pack! We also have these combo packs in Green, Red, Yellow-Green, Blue, and Yellow. This is a nice, bright alphanumeric display that shows letters and numbers in a beautiful hue. It's super bright and designed for viewing from distances up to 23 feet (7 meters) away. Each of the digit sets have 14 segments on a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
