# Fritzing sketch display_zero (saved by Fritzing 0.9.3b)

parts:
  Raspberry_Pi_Zero2 = Raspberry Pi Zero
  Part3 = Adafruit Quad AlphaNumeric Featherwing - White [part_number="Adafruit #3127"]

nets:
  3V3: Raspberry_Pi_Zero2.3v3, Part3.VDD
  N1: Raspberry_Pi_Zero2.GPIO2, Part3.SDA
  N2: Raspberry_Pi_Zero2.GPIO3, Part3.SCL
  GND: Raspberry_Pi_Zero2.GND, Part3.GND

custom parts:
  Adafruit Quad AlphaNumeric Featherwing - White: This is the White Adafruit 0.54" Dual Alphanumeric Display w/ FeatherWing Combo Pack! We also have these combo packs in Green, Red, Yellow-Green, Blue, and Yellow. This is a nice, bright alphanumeric display that shows letters and numbers in a beautiful hue. It's super bright and designed for viewing from distances up to 23 feet (7 meters) away. Each of the digit sets have 14 segments on a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
