# Fritzing sketch pwm_audio_zero (saved by Fritzing 0.9.3b)
breadboards: 1

parts:
  Raspberry_Pi_Zero1 = Raspberry Pi Zero
  R8 = Resistor [tolerance=±5% resistance=270 package=THT]
  R9 = Resistor [tolerance=±5% resistance=270 package=THT]
  C8 = Ceramic Capacitor [capacitance=10nF package="100 mil [THT, multilayer]"]
  C9 = Ceramic Capacitor [capacitance=10nF package="100 mil [THT, multilayer]"]
  R10 = Resistor [tolerance=±5% resistance=150 package=THT]
  R11 = Resistor [tolerance=±5% resistance=150 package=THT]
  C10 = Electrolytic Capacitor [capacitance=1µF package="100 mil [THT, electrolytic]"]
  C11 = Electrolytic Capacitor [capacitance=1µF package="100 mil [THT, electrolytic]"]
  SP2 = SPEAKER [package=pcb_mount_speaker]

nets:
  N1: Raspberry_Pi_Zero1.GND, C8.1, C9.0, R10.Pin_1, R11.Pin_0
  N2: Raspberry_Pi_Zero1.GPIO18, R9.Pin_0
  N3: R8.Pin_1, C8.0, R10.Pin_0, C11.+
  N4: R9.Pin_1, C9.1, R11.Pin_1, C10.+
  N5: C10.-, SP2.+
  N6: C11.-, SP2.-
